# Fritzing sketch PS2 (saved by Fritzing 0.9.2b)
circuit board: 8.46667cm x 5.64444cm
breadboards: 1

parts:
  PS2_port = mini DIN 6 Connector [package=mini-din6]
  Board = Arduino Uno (Rev3)
  R1 = Rotary Potentiometer (Small) [maximum_resistance=100kΩ package=THT]
  LED1 = LED - 5mm [color="Yellow (585nm)" package="5 mm [THT]"]
  R2 = Resistor [tolerance=±5% resistance=220 package=THT]
  R3 = Resistor [tolerance=±20% resistance=220 package=THT]
  LCD = LCD screen
  Buzzer = Piezo Speaker
  STOP_/_SOS = Pushbutton [package="[THT]"]
  R5 = Resistor [tolerance=±5% resistance=10k package=THT]
  R4 = Resistor [tolerance=±5% resistance=220 package=THT]

nets (from the schematic view):
  N1: PS2_port.1, Board.D4
  GND: PS2_port.3, Board.GND, R1.leg1, LED1.cathode, LCD.VSS, LCD.R/W, LCD.LED-, Buzzer.pin1, R5.Pin_0
  N2: PS2_port.5, Board.D3_PWM
  5V: PS2_port.6, Board.5V, R1.leg2, R2.Pin_0, LCD.VDD, STOP_/_SOS.Pin_1, STOP_/_SOS.Pin_2
  N3: Board.D8, LCD.DB6
  N4: Board.D9_PWM, LCD.DB7
  N5: Board.D10_PWM/SS, LCD.RS
  N6: Board.D11_PWM/MOSI, LCD.E
  N7: Board.D13/SCK, R3.Pin_0
  N8: Board.D2, STOP_/_SOS.Pin_3, STOP_/_SOS.Pin_4, R5.Pin_1
  N9: Board.D5_PWM, R4.Pin_1
  N10: Board.D6_PWM, LCD.DB4
  N11: Board.D7, LCD.DB5
  N12: R1.wiper, LCD.V0
  N13: LED1.anode, R3.Pin_1
  N14: R2.Pin_1, LCD.LED+
  N15: Buzzer.pin2, R4.Pin_0
